# Fritzing sketch PSoC5LP_TDA1543 (saved by Fritzing 0.9.3b)
breadboards: 2
perfboards: 2

parts:
  IC1 = IC, DIP package, 8 pins [chip_label=IC]
  R1 = Resistor [tolerance=±5% resistance=1.8k package=THT]
  R2 = Resistor [tolerance=±5% resistance=1.8k package=THT]
  R3 = Resistor [tolerance=±5% resistance=1.5k package=THT]
  C1 = Ceramic Capacitor [capacitance=100nF package="100 mil [THT, multilayer]"]
  C2 = Electrolytic Capacitor [capacitance=1µF package="100 mil [THT, electrolytic]"]
  Power_plug1 = Power plug

nets:
  N1: IC1.pin4, R1.Pin_0, R2.Pin_0, R3.Pin_0, C1.1, C2.-, Power_plug1.GND
  N2: IC1.pin5, C1.0, C2.+, Power_plug1.VCC
  N3: IC1.pin6, R2.Pin_1
  N4: IC1.pin7, R3.Pin_1
  N5: IC1.pin8, R1.Pin_1

notes:
  PSoC 5LP Prototyping Kit
  TDA1543
  1 BCK 8 AOR
  2 WS 7 Vref
  3 DATA 6 AOL
  4 GND 5 VDD
  DC +5V
  R Channel
  L Channel
